// Logisim project MiniCounter.circ as structural Verilog: 21 circuits, main circuit 数码管驱动
// LED计数
module \LED计数电路  (
);


  // Notes on the sheet:
  //   此电路空白，需要你从头绘制！
endmodule

module \LED计数测试  (
);


  // Notes on the sheet:
  //   此电路空白，需要你从头绘制！
endmodule

// 编码器
module \_5输入编码器  (
);


  // Notes on the sheet:
  //   此电路空白，需要你从头绘制！
endmodule

module \数码管驱动  (
  input  X3,
  input  X2,
  input  X1,
  input  X0,
  output Seg_1,
  output Seg_2,
  output Seg_3,
  output Seg_4,
  output Seg_5,
  output Seg_6,
  output Seg_7
);
endmodule

module \数码管驱动测试  (
);

  wire clock_1_out, \数码管驱动_1_seg_1 , \数码管驱动_1_seg_2 , \数码管驱动_1_seg_3 , \数码管驱动_1_seg_4 , \数码管驱动_1_seg_5 ,
       \数码管驱动_1_seg_6 , \数码管驱动_1_seg_7 ;
  wire [3:0] counter_1_q;

  Counter #(.width(4), .max('hf), .ongoal("wrap"), .trigger("rising"), .behavior("old")) counter_1 (
    .Q(counter_1_q), .clk(clock_1_out));  // open: load, D, count, carry, clr, preset
  Clock #(.highDuration(1), .lowDuration(1)) clock_1 (.out(clock_1_out));
  \数码管驱动  \u_数码管驱动_1  (
    .X3(counter_1_q[3]), .Seg_1(\数码管驱动_1_seg_1 ), .X2(counter_1_q[2]), .Seg_2(\数码管驱动_1_seg_2 ),
    .X1(counter_1_q[1]), .Seg_3(\数码管驱动_1_seg_3 ), .X0(counter_1_q[0]), .Seg_4(\数码管驱动_1_seg_4 ),
    .Seg_5(\数码管驱动_1_seg_5 ), .Seg_6(\数码管驱动_1_seg_6 ), .Seg_7(\数码管驱动_1_seg_7 ));
  _7_Segment_Display #(.active("true")) u_7_segment_display_1 (
    .g(\数码管驱动_1_seg_1 ), .f(\数码管驱动_1_seg_2 ), .a(\数码管驱动_1_seg_3 ), .b(\数码管驱动_1_seg_4 ), .e(\数码管驱动_1_seg_5 ),
    .d(\数码管驱动_1_seg_6 ), .c(\数码管驱动_1_seg_7 ));  // open: dp

  // Notes on the sheet:
  //   Ctrl+T驱动时钟单步运行测试
endmodule

// 4位数比较器
module \_4位无符号比较器  (
  input  X3,
  input  X2,
  input  X1,
  input  X0,
  input  Y3,
  input  Y2,
  input  Y1,
  input  Y0,
  output Great,
  output Equal,
  output Less
);
endmodule

module \_8位无符号比较器  (
  input  [7:0] X,
  input  [7:0] Y,
  output Great,
  output Equal,
  output Less
);

  // Probe on X
  // Probe on Y
  \_4位无符号比较器  \u_4位无符号比较器_1  ();  // open: X3, X2, X1, X0, Y3, Y2, Y1, Y0, Great, Equal, Less
  \_4位无符号比较器  \u_4位无符号比较器_2  ();  // open: X3, X2, X1, X0, Y3, Y2, Y1, Y0, Great, Equal, Less

  // Other names for the same wires on the sheet: X0[3:0] = X[3:0]; X1[3:0] = X[7:4]; Y0[3:0] = Y[3:0];
  //   Y1[3:0] = Y[7:4]

  // Notes on the sheet:
  //   请勿增删改引脚，否则可能导致电路封装变化，无法测试
  //   请勿增删改引脚，请在下方利用上方输入输出引脚的隧道标签信号构建电路，ctrl+d复制  选择组件
  //   电路功能：X,Y进行无符号比较，Great=(X>Y)?1:0;
  //   输出引脚区
endmodule

// MUX
module \_2路选择器_1位  (
  input  X0,
  input  Sel,
  input  X1,
  output Out
);


  // Notes on the sheet:
  //   请勿增删改引脚，否则可能导致电路封装变化，无法测试
  //   请勿增删改引脚，请在下方利用上方输入输出引脚的隧道标签信号构建电路，ctrl+d复制  选择组件
  //   输入引脚区
  //   输出引脚区
  //   电路功能：Out=(Sel==0)?X0:X1;
endmodule

// MUX
module \_2路选择器_4位  (
  input  [3:0] X,
  input  Sel,
  input  [3:0] Y,
  output [3:0] Out
);

  // Probe on X
  // Probe on Y
  // Probe on Out

  // Notes on the sheet:
  //   请勿增删改引脚，否则可能导致电路封装变化，无法测试！
  //   请勿增删改引脚，请在下方利用上方输入输出引脚的隧道标签信号构建电路，ctrl+d复制  选择组件
  //   输入引脚区
  //   电路功能：Out=(Sel==0)?X:Y;
  //   输出引脚区
endmodule

// BCD计数
module \BCD双向计数器_可异步置位  (
  input  CLK,
  input  \使能 ,
  input  \异步置位 ,
  input  [3:0] \预置数据 ,
  input  \计数模式 ,
  input  \复位 ,
  output [3:0] \输出Q ,
  output \进位_借位 
);

  wire D0, D1, D2, D3, or_1_out;
  wire [3:0] \n2路选择器_4位_1_out ;

  Pull_Resistor #(.pull(0)) pull_resistor_1 (.node(\异步置位 ));
  Pull_Resistor #(.pull(0)) pull_resistor_2 (.node(\计数模式 ));
  \BCD双向计数器状态转换_自动生成  \bcd双向计数器状态转换_自动生成_1  ();  // open: S3, N3, S2, N2, S1, N1, S0, N0, Mode
  \BCD双向计数器输出函数_自动生成  \bcd双向计数器输出函数_自动生成_1  (.Cout(\进位_借位 ));  // open: S3, S2, S1, S0, Mode
  Pull_Resistor #(.pull(1)) pull_resistor_3 (.node(\使能 ));
  Pull_Resistor #(.pull(0)) pull_resistor_4 (.node(\预置数据 ));
  Pull_Resistor #(.pull(0)) pull_resistor_5 (.node(\复位 ));
  \_2路选择器_4位  \u_2路选择器_4位_1  (.X(\预置数据 ), .Out(\n2路选择器_4位_1_out ), .Sel(\复位 ), .Y(4'b0000));
  D_Flip_Flop #(.trigger("rising"), .Pre_Clr_Positions("LEGACY"), .NegatePresetClear("false"), .enable("true"), .NewFFLayout("false")) u_D3 ();  // open: clk, D, Q, Qn, preset, en, reset
  D_Flip_Flop #(.trigger("rising"), .Pre_Clr_Positions("LEGACY"), .NegatePresetClear("false"), .enable("true"), .NewFFLayout("false")) u_D2 ();  // open: clk, D, Q, Qn, preset, en, reset
  D_Flip_Flop #(.trigger("rising"), .Pre_Clr_Positions("LEGACY"), .NegatePresetClear("false"), .enable("true"), .NewFFLayout("false")) u_D1 ();  // open: clk, D, Q, Qn, preset, en, reset
  D_Flip_Flop #(.trigger("rising"), .Pre_Clr_Positions("LEGACY"), .NegatePresetClear("false"), .enable("true"), .NewFFLayout("false")) u_D0 ();  // open: clk, D, Q, Qn, preset, en, reset
  assign {D3, D2, D1, D0} = or_1_out ? \n2路选择器_4位_1_out  : 4'bz;  // Controlled_Buffer controlled_buffer_1
  or or_1 (or_1_out, \复位 , \异步置位 );
  // Probe on \输出Q 

  // Other names for the same wires on the sheet: Cout = \进位_借位 ; Din[3:0] = \预置数据 ; En = \使能 ; Mode = \计数模式 ;
  //   PreSet = \异步置位 ; Q[3:0] = \输出Q ; RST = \复位 

  // Notes on the sheet:
  //   请勿增删改引脚，否则可能导致电路封装变化，无法测试！！！
  //   上拉下拉电阻用于给出引脚悬空的时的默认值
  //   D3D2D1D0分别接D触发器异步置位和复位端实现异步置位
  //   正计数到9，倒计数到0时输出为1
endmodule

// 状态转换
module \BCD双向计数器状态转换_自动生成  (
  input  S3,
  input  S2,
  input  S1,
  input  S0,
  input  Mode,
  output N3,
  output N2,
  output N1,
  output N0
);
endmodule

module \BCD双向计数器输出函数_自动生成  (
  input  S3,
  input  S2,
  input  S1,
  input  S0,
  input  Mode,
  output Cout
);
endmodule

// 0~5计数
module \_0_5双向计数器_可异步置位  (
  input  CLK,
  input  \使能 ,
  input  \异步置位 ,
  input  [3:0] \预置数据 ,
  input  \计数模式 ,
  input  RST,
  output [3:0] \输出Q ,
  output \进位_借位 
);

  wire D0, D1, D2, D3, or_1_out;
  wire [3:0] \n2路选择器_4位_1_out ;

  Pull_Resistor #(.pull(0)) pull_resistor_1 (.node(\异步置位 ));
  Pull_Resistor #(.pull(0)) pull_resistor_2 (.node(\计数模式 ));
  \_0_5双向计数器输出函数_自动生成  \u_0_5双向计数器输出函数_自动生成_1  ();  // open: S3, Cout, S2, S1, S0, Mode
  \_0_5双向计数器状态转换_自动生成  \u_0_5双向计数器状态转换_自动生成_1  ();  // open: S3, N3, S2, N2, S1, N1, S0, N0, Mode
  Pull_Resistor #(.pull(1)) pull_resistor_3 (.node(\使能 ));
  Pull_Resistor #(.pull(0)) pull_resistor_4 (.node(\预置数据 ));
  Pull_Resistor #(.pull(0)) pull_resistor_5 (.node(RST));
  D_Flip_Flop #(.trigger("rising"), .Pre_Clr_Positions("LEGACY"), .NegatePresetClear("false"), .enable("true"), .NewFFLayout("false")) u_D3 ();  // open: clk, D, Q, Qn, preset, en, reset
  D_Flip_Flop #(.trigger("rising"), .Pre_Clr_Positions("LEGACY"), .NegatePresetClear("false"), .enable("true"), .NewFFLayout("false")) u_D2 ();  // open: clk, D, Q, Qn, preset, en, reset
  D_Flip_Flop #(.trigger("rising"), .Pre_Clr_Positions("LEGACY"), .NegatePresetClear("false"), .enable("true"), .NewFFLayout("false")) u_D1 ();  // open: clk, D, Q, Qn, preset, en, reset
  D_Flip_Flop #(.trigger("rising"), .Pre_Clr_Positions("LEGACY"), .NegatePresetClear("false"), .enable("true"), .NewFFLayout("false")) u_D0 ();  // open: clk, D, Q, Qn, preset, en, reset
  \_2路选择器_4位  \u_2路选择器_4位_1  (.X(\预置数据 ), .Out(\n2路选择器_4位_1_out ), .Sel(RST), .Y(4'b0000));
  assign {D3, D2, D1, D0} = or_1_out ? \n2路选择器_4位_1_out  : 4'bz;  // Controlled_Buffer controlled_buffer_1
  or or_1 (or_1_out, RST, \异步置位 );
  // Probe on \输出Q 

  // Other names for the same wires on the sheet: Cout = \进位_借位 ; Din[3:0] = \预置数据 ; En = \使能 ; Mode = \计数模式 ;
  //   PreSet = \异步置位 ; Q[3:0] = \输出Q 

  // Notes on the sheet:
  //   请勿增删改引脚，否则可能导致电路封装变化，无法测试！！！
  //   上拉下拉电阻用于给出引脚悬空的时的默认值
  //   D3D2D1D0分别接D触发器异步置位和复位端实现异步置位
  //   正计数到9，倒计数到0时输出为1
endmodule

// 状态转换
module \_0_5双向计数器状态转换_自动生成  (
  input  S3,
  input  S2,
  input  S1,
  input  S0,
  input  Mode,
  output N3,
  output N2,
  output N1,
  output N0
);
endmodule

module \_0_5双向计数器输出函数_自动生成  (
  input  S3,
  input  S2,
  input  S1,
  input  S0,
  input  Mode,
  output Cout
);
endmodule

// 0~59双向计数
module \_0_59双向计数器  (
  input  CLK,
  input  \使能 ,
  input  \异步置位 ,
  input  [7:0] \预置数据 ,
  input  \计数模式 ,
  input  RST,
  output [7:0] \输出Q ,
  output \进位_借位 
);

  Pull_Resistor #(.pull(0)) pull_resistor_1 (.node(\异步置位 ));
  Pull_Resistor #(.pull(0)) pull_resistor_2 (.node(\计数模式 ));
  \_0_5双向计数器_可异步置位  \u_0_5双向计数器_可异步置位_1  ();  // open: CLK, 使能, 异步置位, 预置数据, 计数模式, 输出Q, 进位_借位, RST
  Pull_Resistor #(.pull(1)) pull_resistor_3 (.node(\使能 ));
  Pull_Resistor #(.pull(0)) pull_resistor_4 (.node(\预置数据 ));
  Pull_Resistor #(.pull(0)) pull_resistor_5 (.node(RST));
  \BCD双向计数器_可异步置位  \bcd双向计数器_可异步置位_1  ();  // open: CLK, 使能, 输出Q, 异步置位, 预置数据, 进位_借位, 计数模式, 复位

  // Other names for the same wires on the sheet: Cout = \进位_借位 ; Din[7:0] = \预置数据 ; Din0[3:0] = \预置数据 [3:0];
  //   Din1[3:0] = \预置数据 [7:4]; En = \使能 ; Mode = \计数模式 ; PreSet = \异步置位 ; Q[7:0] = \输出Q 

  // Notes on the sheet:
  //   请勿增删改引脚，否则可能导致电路封装变化，无法测试！！！
  //   正计数到59，倒计数到0时输出为1
endmodule

// 倒计数
module \_59分59秒双向计数器  (
  input  CLK,
  input  \使能 ,
  input  \异步置位 ,
  input  [15:0] \预置数据 ,
  input  \计数模式 ,
  input  RST,
  output [7:0] Minute,
  output [7:0] Second,
  output \进位_借位 
);

  Pull_Resistor #(.pull(0)) pull_resistor_1 (.node(\异步置位 ));
  Pull_Resistor #(.pull(0)) pull_resistor_2 (.node(\计数模式 ));
  \_0_59双向计数器  \u_0_59双向计数器_1  ();  // open: CLK, 使能, 输出Q, 异步置位, 预置数据, 进位_借位, 计数模式, RST
  Pull_Resistor #(.pull(1)) pull_resistor_3 (.node(\使能 ));
  Pull_Resistor #(.pull(0)) pull_resistor_4 (.node(\预置数据 ));
  Pull_Resistor #(.pull(0)) pull_resistor_5 (.node(RST));
  \_0_59双向计数器  \u_0_59双向计数器_2  ();  // open: CLK, 使能, 输出Q, 异步置位, 预置数据, 进位_借位, 计数模式, RST

  // Other names for the same wires on the sheet: Cout = \进位_借位 ; Din[15:0] = \预置数据 ; SDin[7:0] = \预置数据 [7:0];
  //   MDin[7:0] = \预置数据 [15:8]; En = \使能 ; Min[7:0] = Minute; Mode = \计数模式 ; PreSet = \异步置位 ; Sec[7:0] = Second

  // Notes on the sheet:
  //   请勿增删改引脚，否则可能导致电路封装变化，无法测试！！！
  //   正计数到59：59，倒计数到0时输出为1
endmodule

// 状态机
module \厨房计时器状态机  (
  input  S2,
  input  S1,
  input  S0,
  input  mode,
  input  start,
  input  timer,
  input  AlertDone,
  output N2,
  output N1,
  output N0
);
endmodule

// 输出
module \厨房计时器输出函数  (
  input  S2,
  input  S1,
  input  S0,
  output Preset,
  output CounterEn,
  output AlertTimerEnable,
  output Runing
);
endmodule

module \厨房计时器  (
  input  EduMin,
  input  EduStart,
  input  EduSec,
  input  EduReset,
  output [2:0] Status,
  output [15:0] \当前时间 ,
  output \正在报警 
);

  wire _0_5HZ, _2HZ, _4HZ, _16HZ, and_1_out, and_2_out, \bcd双向计数器_可异步置位_1_进位_借位 , buzzer_1_p9,
       \n59分59秒双向计数器_1_进位_借位 , undriven, undriven_2, undriven_4, undriven_5, undriven_6, undriven_9,
       undriven_12, \分 , \分_t , \厨房计时器输出函数_1_counteren , \厨房计时器输出函数_1_preset , \厨房计时器输出函数_1_runing , \开始_暂停 ,
       \开始_暂停_t , \归零 , \归零_t , \秒 , \秒_t ;
  wire [0:0] counter_1_q;
  wire [2:0] S1B, S2B, S3B, S4B, undriven_3, undriven_7, \厨房计时器状态机_1_n0 ;
  wire [3:0] \bcd双向计数器_可异步置位_1_输出q , S1T, S2T, S3T, S4T;
  wire [6:0] undriven_10, undriven_11;
  wire [7:0] \n0_59双向计数器_1_输出q , \n0_59双向计数器_2_输出q ;
  wire [15:0] undriven_8;

  _7_Segment_Display #(.active("true")) u_7_segment_display_1 (
    .g(S4T[0]), .f(S4T[1]), .a(S4T[2]), .b(S4T[3]), .e(S4B[0]), .d(S4B[1]), .c(S4B[2]));  // open: dp
  _7_Segment_Display #(.active("true")) u_7_segment_display_2 (
    .g(S3T[0]), .f(S3T[1]), .a(S3T[2]), .b(S3T[3]), .e(S3B[0]), .d(S3B[1]), .c(S3B[2]));  // open: dp
  _7_Segment_Display #(.active("true")) u_7_segment_display_3 (
    .g(S2T[0]), .f(S2T[1]), .a(S2T[2]), .b(S2T[3]), .e(S2B[0]), .d(S2B[1]), .c(S2B[2]));  // open: dp
  Button button_1 (.out(\分_t ));
  _7_Segment_Display #(.active("true")) u_7_segment_display_4 (
    .g(S1T[0]), .f(S1T[1]), .a(S1T[2]), .b(S1T[3]), .e(S1B[0]), .d(S1B[1]), .c(S1B[2]));  // open: dp
  Button button_2 (.out(\开始_暂停_t ));
  // Probe on \bcd双向计数器_可异步置位_1_输出q 
  \BCD双向计数器_可异步置位  \bcd双向计数器_可异步置位_1  (
    .\输出Q (\bcd双向计数器_可异步置位_1_输出q ), .\进位_借位 (\bcd双向计数器_可异步置位_1_进位_借位 ));  // open: CLK, 使能, 异步置位, 预置数据, 计数模式, 复位
  Button button_3 (.out(\秒_t ));
  Button button_4 (.out(\归零_t ));
  Clock #(.highDuration(1), .lowDuration(1)) clock_1 (.out(_16HZ));
  \厨房计时器状态机  \u_厨房计时器状态机_1  (
    .S2(undriven_3[2]), .N2(\厨房计时器状态机_1_n0 [2]), .S1(undriven_3[1]), .N1(\厨房计时器状态机_1_n0 [1]),
    .S0(undriven_3[0]), .N0(\厨房计时器状态机_1_n0 [0]), .mode(undriven), .start(undriven_2), .timer(undriven_4),
    .AlertDone(undriven_5));
  Counter #(.width(3), .max('h7), .ongoal("wrap"), .trigger("rising"), .behavior("new")) counter_1 (
    .count(undriven_6), .Q({_2HZ, _4HZ, counter_1_q[0]}), .clk(_16HZ), .preset(undriven_6));  // open: load, D, carry, clr, down
  Register #(.width(3), .trigger("rising"), .Select("low")) register_1 (.Q(Status));  // open: D, en, clk, clr
  \厨房计时器输出函数  \u_厨房计时器输出函数_1  (
    .S2(undriven_7[2]), .S1(undriven_7[1]), .S0(undriven_7[0]), .Preset(\厨房计时器输出函数_1_preset ),
    .CounterEn(\厨房计时器输出函数_1_counteren ), .AlertTimerEnable(\正在报警 ), .Runing(\厨房计时器输出函数_1_runing ));
  // Probe on \n0_59双向计数器_1_输出q 
  \_0_59双向计数器  \u_0_59双向计数器_1  (.\输出Q (\n0_59双向计数器_1_输出q ));  // open: CLK, 使能, 异步置位, 预置数据, 进位_借位, 计数模式, RST
  // Probe on \n0_59双向计数器_2_输出q 
  \_0_59双向计数器  \u_0_59双向计数器_2  (.\输出Q (\n0_59双向计数器_2_输出q ));  // open: CLK, 使能, 异步置位, 预置数据, 进位_借位, 计数模式, RST
  and and_1 (and_1_out, \正在报警 , _2HZ);
  // Buzzer #(.freq_measure("Hz"), .vol_width(7)) buzzer_1: pin names not known; wires that end beside it: _16HZ, \厨房计时器输出函数_1_preset , \厨房计时器输出函数_1_runing , \厨房计时器输出函数_1_counteren , \正在报警 , 14'h1000, and_1_out, {7{1'b1}}, buzzer_1_p9, \当前时间 [15:8], \当前时间 [7:0]
  \_59分59秒双向计数器  \u_59分59秒双向计数器_1  (
    .Minute(\当前时间 [15:8]), .\进位_借位 (\n59分59秒双向计数器_1_进位_借位 ), .Second(\当前时间 [7:0]), .\异步置位 (buzzer_1_p9),
    .\预置数据 (undriven_8), .\计数模式 (undriven_9));  // open: CLK, 使能, RST
  or or_1 (\分 , EduMin, \分_t );
  or or_2 (\秒 , EduSec, \秒_t );
  or or_3 (\开始_暂停 , EduStart, \开始_暂停_t );
  or or_4 (\归零 , EduReset, \归零_t );
  \数码管驱动  \u_数码管驱动_1  ();  // open: X3, Seg_1, X2, Seg_2, X1, Seg_3, X0, Seg_4, Seg_5, Seg_6, Seg_7
  \数码管驱动  \u_数码管驱动_2  ();  // open: X3, Seg_1, X2, Seg_2, X1, Seg_3, X0, Seg_4, Seg_5, Seg_6, Seg_7
  \数码管驱动  \u_数码管驱动_3  ();  // open: X3, Seg_1, X2, Seg_2, X1, Seg_3, X0, Seg_4, Seg_5, Seg_6, Seg_7
  \数码管驱动  \u_数码管驱动_4  ();  // open: X3, Seg_1, X2, Seg_2, X1, Seg_3, X0, Seg_4, Seg_5, Seg_6, Seg_7
  Multiplexer #(.select(1), .width(7), .disabled("Z"), .enable("false")) multiplexer_1 (
    .in0(undriven_10), .in1(undriven_11), .out({S4B, S4T}), .sel(undriven_12));
  and and_2 (and_2_out, \正在报警 , _0_5HZ);

  // Other names for the same wires on the sheet: Alert = \正在报警 ; Sec[7:0] = \当前时间 [7:0]; Min[7:0] = \当前时间 [15:8];
  //   当前状态[2:0] = Status

  // Notes on the sheet:
  //   警铃计时或倒计时
  //   厨房计时器
  //   分频电路
  //   线上评测前请将蜂鸣器删除！
  //   蜂鸣器
  //   倒计时到0时间闪烁控制
endmodule

module \子电路外观测试  (
);

  wire _1HZ, \bcd双向计数器状态转换_自动生成_1_n0 , \bcd双向计数器状态转换_自动生成_1_n1 , \bcd双向计数器状态转换_自动生成_1_n2 ,
       \bcd双向计数器状态转换_自动生成_1_n3 , \bcd双向计数器输出函数_自动生成_1_cout , CLK, clock_1_out, Cout, EN, En_t, Mode,
       \n0_5双向计数器状态转换_自动生成_1_n0 , \n0_5双向计数器状态转换_自动生成_1_n1 , \n0_5双向计数器状态转换_自动生成_1_n2 ,
       \n0_5双向计数器状态转换_自动生成_1_n3 , \n0_5双向计数器输出函数_自动生成_1_cout , \n2路选择器_1位_1_out , \n4位无符号比较器_1_equal ,
       \n4位无符号比较器_1_great , \n4位无符号比较器_1_less , \n8位无符号比较器_1_equal , \n8位无符号比较器_1_great , \n8位无符号比较器_1_less ,
       PreSet, Preset_t, RST, undriven, undriven_2, undriven_3, undriven_6, undriven_7, undriven_8,
       undriven_9, undriven_10, undriven_11, undriven_12, undriven_13, undriven_14, undriven_15, undriven_16,
       undriven_19, undriven_20, undriven_21, undriven_22, undriven_23, undriven_24, undriven_25,
       undriven_26, undriven_27, undriven_28, undriven_29, undriven_30, undriven_31, undriven_32,
       undriven_33, undriven_34, undriven_35, undriven_36, undriven_37, \倒计时 , \厨房计时器状态机_1_n0 ,
       \厨房计时器状态机_1_n1 , \厨房计时器状态机_1_n2 , \厨房计时器输出函数_1_alerttimerenable , \厨房计时器输出函数_1_counteren ,
       \厨房计时器输出函数_1_preset , \厨房计时器输出函数_1_runing , \归零 ;
  wire [3:0] counter_1_q, Din0, Din1, \n2路选择器_4位_1_out , Timer1, Timer2, undriven_4, undriven_5, X1, Y1;
  wire [6:0] \数码管驱动_1_seg_1 ;
  wire [7:0] MDin, Min, Sec, Timer, undriven_17, undriven_18;
  wire [15:0] Din;

  Counter #(.width(4), .max('hf), .ongoal("wrap"), .trigger("rising"), .behavior("old")) counter_1 (
    .Q(counter_1_q), .clk(clock_1_out));  // open: load, D, count, carry, clr, preset
  Clock #(.highDuration(1), .lowDuration(1)) clock_1 (.out(clock_1_out));
  \数码管驱动  \u_数码管驱动_1  (
    .X3(counter_1_q[3]), .Seg_1(\数码管驱动_1_seg_1 [0]), .X2(counter_1_q[2]), .Seg_2(\数码管驱动_1_seg_1 [1]),
    .X1(counter_1_q[1]), .Seg_3(\数码管驱动_1_seg_1 [2]), .X0(counter_1_q[0]), .Seg_4(\数码管驱动_1_seg_1 [3]),
    .Seg_5(\数码管驱动_1_seg_1 [4]), .Seg_6(\数码管驱动_1_seg_1 [5]), .Seg_7(\数码管驱动_1_seg_1 [6]));
  \_2路选择器_1位  \u_2路选择器_1位_1  (.X0(undriven), .Sel(undriven_3), .Out(\n2路选择器_1位_1_out ), .X1(undriven_2));
  // Probe on Timer2
  \BCD双向计数器_可异步置位  \bcd双向计数器_可异步置位_1  (
    .CLK(CLK), .\使能 (En_t), .\输出Q (Timer2), .\异步置位 (PreSet), .\预置数据 (Din0), .\进位_借位 (Cout), .\计数模式 (Mode),
    .\复位 (RST));
  \_0_59双向计数器  \u_0_59双向计数器_1  (
    .CLK(CLK), .\使能 (En_t), .\输出Q (Timer), .\异步置位 (PreSet), .\预置数据 (MDin), .\进位_借位 (Cout), .\计数模式 (Mode),
    .RST(RST));
  \_2路选择器_4位  \u_2路选择器_4位_1  (.X(undriven_4), .Out(\n2路选择器_4位_1_out ), .Sel(undriven_6), .Y(undriven_5));
  \_4位无符号比较器  \u_4位无符号比较器_1  (
    .X3(X1[3]), .X2(X1[2]), .X1(X1[1]), .X0(X1[0]), .Y3(Y1[3]), .Y2(Y1[2]), .Y1(Y1[1]), .Y0(Y1[0]),
    .Great(\n4位无符号比较器_1_great ), .Equal(\n4位无符号比较器_1_equal ), .Less(\n4位无符号比较器_1_less ));
  \BCD双向计数器状态转换_自动生成  \bcd双向计数器状态转换_自动生成_1  (
    .S3(undriven_7), .N3(\bcd双向计数器状态转换_自动生成_1_n3 ), .S2(undriven_8), .N2(\bcd双向计数器状态转换_自动生成_1_n2 ),
    .S1(undriven_9), .N1(\bcd双向计数器状态转换_自动生成_1_n1 ), .S0(undriven_10), .N0(\bcd双向计数器状态转换_自动生成_1_n0 ),
    .Mode(undriven_11));
  \BCD双向计数器输出函数_自动生成  \bcd双向计数器输出函数_自动生成_1  (
    .S3(undriven_12), .Cout(\bcd双向计数器输出函数_自动生成_1_cout ), .S2(undriven_13), .S1(undriven_14),
    .S0(undriven_15), .Mode(undriven_16));
  \_0_5双向计数器_可异步置位  \u_0_5双向计数器_可异步置位_1  (
    .CLK(CLK), .\使能 (En_t), .\异步置位 (PreSet), .\预置数据 (Din1), .\计数模式 (Mode), .\输出Q (Timer1), .\进位_借位 (Cout),
    .RST(RST));
  \_59分59秒双向计数器  \u_59分59秒双向计数器_1  (
    .Minute(Min), .\进位_借位 (Cout), .Second(Sec), .CLK(_1HZ), .\使能 (EN), .\异步置位 (Preset_t), .\预置数据 (Din),
    .\计数模式 (\倒计时 ), .RST(\归零 ));
  \_8位无符号比较器  \u_8位无符号比较器_1  (
    .Great(\n8位无符号比较器_1_great ), .X(undriven_17), .Equal(\n8位无符号比较器_1_equal ), .Y(undriven_18),
    .Less(\n8位无符号比较器_1_less ));
  \_0_5双向计数器状态转换_自动生成  \u_0_5双向计数器状态转换_自动生成_1  (
    .S3(undriven_19), .N3(\n0_5双向计数器状态转换_自动生成_1_n3 ), .S2(undriven_20), .N2(\n0_5双向计数器状态转换_自动生成_1_n2 ),
    .S1(undriven_21), .N1(\n0_5双向计数器状态转换_自动生成_1_n1 ), .S0(undriven_22), .N0(\n0_5双向计数器状态转换_自动生成_1_n0 ),
    .Mode(undriven_23));
  \厨房计时器状态机  \u_厨房计时器状态机_1  (
    .S2(undriven_24), .N2(\厨房计时器状态机_1_n2 ), .S1(undriven_25), .N1(\厨房计时器状态机_1_n1 ), .S0(undriven_26),
    .N0(\厨房计时器状态机_1_n0 ), .mode(undriven_27), .start(undriven_28), .timer(undriven_29),
    .AlertDone(undriven_30));
  \_0_5双向计数器输出函数_自动生成  \u_0_5双向计数器输出函数_自动生成_1  (
    .S3(undriven_31), .Cout(\n0_5双向计数器输出函数_自动生成_1_cout ), .S2(undriven_32), .S1(undriven_32),
    .S0(undriven_33), .Mode(undriven_34));
  \厨房计时器输出函数  \u_厨房计时器输出函数_1  (
    .S2(undriven_36), .S1(undriven_35), .S0(undriven_37), .Preset(\厨房计时器输出函数_1_preset ),
    .CounterEn(\厨房计时器输出函数_1_counteren ), .AlertTimerEnable(\厨房计时器输出函数_1_alerttimerenable ),
    .Runing(\厨房计时器输出函数_1_runing ));
endmodule
